// Digital circuit And.dig as structural Verilog
module And (
  input  a,
  input  b,
  output out
);

  wire nand_1_out;

  nand nand_1 (nand_1_out, a, b);
  not not_1 (out, nand_1_out);
endmodule

/* Test case Test1:
a b out
0 0 0
0 1 0
1 0 0
1 1 1
*/
