// Digital circuit DMux.dig as structural Verilog
module DMux (
  input  in,
  input  sel,
  output a,
  output b
);

  wire not_1_out;

  not not_1 (not_1_out, sel);
  and and_1 (a, not_1_out, in);
  and and_2 (b, sel, in);
endmodule

/* Test case Test1:
sel in a b
0 0 0 0
0 1 1 0
1 0 0 0 
1 1 0 1
*/
