// Digital circuit Mux.dig as structural Verilog
module Mux (
  input  a,
  input  b,
  input  sel,
  output out
);

  wire and_1_out, and_2_out, not_1_out;

  and and_1 (and_1_out, a, not_1_out);
  not not_1 (not_1_out, sel);
  and and_2 (and_2_out, sel, b);
  or or_1 (out, and_1_out, and_2_out);
endmodule
