// Digital circuit Or.dig as structural Verilog
module Or (
  input  a,
  input  b,
  output out
);

  wire not_1_out, not_2_out;

  Not not_1 (.in(a), .out(not_1_out));
  Not not_2 (.in(b), .out(not_2_out));
  nand nand_1 (out, not_1_out, not_2_out);
endmodule
