// Digital circuit Register.dig as structural Verilog
module Register (
  input  C,
  input  [15:0] in,
  input  load,
  output [15:0] out
);

  // Probe on C
  // Probe on load
  Register #(.Bits(16)) Reg (.D(in), .C(C), .en(load), .Q(out));
endmodule

/* Test case test1:
C in load out
C 0 0 0
C 0 1 0
C 0x8285 0 0
C 11111 0 0
C 0x8285 1 0x8285
C 0x8285 1 0x8285
0 0x8285 1 0x8285
C 0x8285 0 0x8285
0 12345 1 0x8285
1 12345 1 12345
*/
