// Digital circuit ALU.dig as structural Verilog
module ALU (
  input  [15:0] x,
  input  [15:0] y,
  input  zx,
  input  nx,
  input  f,
  input  no,
  input  zy,
  input  ny,
  output [15:0] out,
  output zr,
  output ng
);

  wire [15:0] Adder_s, and_1_out, multiplexer_1_out, multiplexer_2_out, multiplexer_3_out, multiplexer_4_out,
       multiplexer_5_out, not_1_out, not_2_out, not_3_out;

  Multiplexer #(.Bits(16)) multiplexer_1 (.sel(zx), .in_0(x), .in_1({16{1'b0}}), .out(multiplexer_1_out));
  Multiplexer #(.Bits(16)) multiplexer_2 (.sel(zy), .in_0(y), .in_1({16{1'b0}}), .out(multiplexer_2_out));
  assign not_1_out = ~multiplexer_1_out;  // Not not_1, 16 bits wide
  assign not_2_out = ~multiplexer_2_out;  // Not not_2, 16 bits wide
  Multiplexer #(.Bits(16)) multiplexer_3 (
    .sel(nx), .in_0(multiplexer_1_out), .in_1(not_1_out), .out(multiplexer_3_out));
  Multiplexer #(.Bits(16)) multiplexer_4 (
    .sel(ny), .in_0(multiplexer_2_out), .in_1(not_2_out), .out(multiplexer_4_out));
  assign and_1_out = multiplexer_3_out & multiplexer_4_out;  // And and_1, 16 bits wide
  Add #(.Bits(16)) Adder (.a(multiplexer_3_out), .b(multiplexer_4_out), .c_i(1'b0), .s(Adder_s));  // open: c_o
  Multiplexer #(.Bits(16)) multiplexer_5 (.sel(f), .in_0(and_1_out), .in_1(Adder_s), .out(multiplexer_5_out));
  assign not_3_out = ~multiplexer_5_out;  // Not not_3, 16 bits wide
  Multiplexer #(.Bits(16)) multiplexer_6 (.sel(no), .in_0(multiplexer_5_out), .in_1(not_3_out), .out(out));
  BitSelector #(.Selector_Bits(4)) bitselector_1 (.in(out), .sel(4'b1111), .out(ng));
  Comparator #(.Bits(16)) comparator_1 (.a(out), .b({16{1'b0}}), .eq(zr));  // open: gt, lt
endmodule

/* Test case test1:
         x                  y          zx  nx  zy  ny   f  no         out         zr  ng  
  0b0000000000000000   0b1111111111111111   1   0   1   0   1   0   0b0000000000000000   1   0  
  0b0000000000000000   0b1111111111111111   1   1   1   1   1   1   0b0000000000000001   0   0  
  0b0000000000000000   0b1111111111111111   1   1   1   0   1   0   0b1111111111111111   0   1  
  0b0000000000000000   0b1111111111111111   0   0   1   1   0   0   0b0000000000000000   1   0  
  0b0000000000000000   0b1111111111111111   1   1   0   0   0   0   0b1111111111111111   0   1  
  0b0000000000000000   0b1111111111111111   0   0   1   1   0   1   0b1111111111111111   0   1  
  0b0000000000000000   0b1111111111111111   1   1   0   0   0   1   0b0000000000000000   1   0  
  0b0000000000000000   0b1111111111111111   0   0   1   1   1   1   0b0000000000000000   1   0  
  0b0000000000000000   0b1111111111111111   1   1   0   0   1   1   0b0000000000000001   0   0  
  0b0000000000000000   0b1111111111111111   0   1   1   1   1   1   0b0000000000000001   0   0  
  0b0000000000000000   0b1111111111111111   1   1   0   1   1   1   0b0000000000000000   1   0  
  0b0000000000000000   0b1111111111111111   0   0   1   1   1   0   0b1111111111111111   0   1  
  0b0000000000000000   0b1111111111111111   1   1   0   0   1   0   0b1111111111111110   0   1  
  0b0000000000000000   0b1111111111111111   0   0   0   0   1   0   0b1111111111111111   0   1  
  0b0000000000000000   0b1111111111111111   0   1   0   0   1   1   0b0000000000000001   0   0  
  0b0000000000000000   0b1111111111111111   0   0   0   1   1   1   0b1111111111111111   0   1  
  0b0000000000000000   0b1111111111111111   0   0   0   0   0   0   0b0000000000000000   1   0  
  0b0000000000000000   0b1111111111111111   0   1   0   1   0   1   0b1111111111111111   0   1  
  0b0000000000010001   0b0000000000000011   1   0   1   0   1   0   0b0000000000000000   1   0  
  0b0000000000010001   0b0000000000000011   1   1   1   1   1   1   0b0000000000000001   0   0  
  0b0000000000010001   0b0000000000000011   1   1   1   0   1   0   0b1111111111111111   0   1  
  0b0000000000010001   0b0000000000000011   0   0   1   1   0   0   0b0000000000010001   0   0  
  0b0000000000010001   0b0000000000000011   1   1   0   0   0   0   0b0000000000000011   0   0  
  0b0000000000010001   0b0000000000000011   0   0   1   1   0   1   0b1111111111101110   0   1  
  0b0000000000010001   0b0000000000000011   1   1   0   0   0   1   0b1111111111111100   0   1  
  0b0000000000010001   0b0000000000000011   0   0   1   1   1   1   0b1111111111101111   0   1  
  0b0000000000010001   0b0000000000000011   1   1   0   0   1   1   0b1111111111111101   0   1  
  0b0000000000010001   0b0000000000000011   0   1   1   1   1   1   0b0000000000010010   0   0  
  0b0000000000010001   0b0000000000000011   1   1   0   1   1   1   0b0000000000000100   0   0  
  0b0000000000010001   0b0000000000000011   0   0   1   1   1   0   0b0000000000010000   0   0  
  0b0000000000010001   0b0000000000000011   1   1   0   0   1   0   0b0000000000000010   0   0  
  0b0000000000010001   0b0000000000000011   0   0   0   0   1   0   0b0000000000010100   0   0  
  0b0000000000010001   0b0000000000000011   0   1   0   0   1   1   0b0000000000001110   0   0  
  0b0000000000010001   0b0000000000000011   0   0   0   1   1   1   0b1111111111110010   0   1  
  0b0000000000010001   0b0000000000000011   0   0   0   0   0   0   0b0000000000000001   0   0  
  0b0000000000010001   0b0000000000000011   0   1   0   1   0   1   0b0000000000010011   0   0  
*/
