// Digital circuit CPU.dig as structural Verilog
module CPU (
  input  [15:0] inM,
  input  [15:0] instruction,
  input  reset,
  input  C,
  output [15:0] outM,
  output writeM,
  output [14:0] addressM,
  output [14:0] pc
);

  wire aIns, aluF, aluNg, aluNo, aluNx, aluNy, aluZr, aluZx, aluZy, and_1_out, and_16_out, and_17_out,
       and_18_out, cIns, destA, destD, jmpEq, jmpGt, jmpLt, not_2_out, or_1_out, or_2_out, or_3_out,
       or_4_out, srcM;
  wire [15:0] Dregister_q, multiplexer_1_out, multiplexer_2_out;
  wire [15:15] Areg, pc_1_out;

  and and_1 (and_1_out, instruction[14], instruction[15]);
  and and_2 (jmpGt, cIns, instruction[0]);
  and and_3 (jmpEq, cIns, instruction[1]);
  and and_4 (jmpLt, cIns, instruction[2]);
  and and_5 (writeM, cIns, instruction[3]);
  and and_6 (destD, cIns, instruction[4]);
  and and_7 (destA, cIns, instruction[5]);
  and and_8 (aluNo, cIns, instruction[6]);
  and and_9 (aluF, cIns, instruction[7]);
  and and_10 (aluNy, cIns, instruction[8]);
  and and_11 (aluZy, cIns, instruction[9]);
  and and_12 (aluNx, cIns, instruction[10]);
  and and_13 (aluZx, cIns, instruction[11]);
  and and_14 (srcM, instruction[12], cIns);
  and and_15 (cIns, instruction[13], and_1_out);
  not not_1 (aIns, instruction[15]);
  and and_16 (and_16_out, jmpLt, aluNg);
  Multiplexer #(.Bits(16)) multiplexer_1 (.sel(aIns), .in_0(outM), .in_1(instruction), .out(multiplexer_1_out));
  and and_17 (and_17_out, jmpEq, aluZr);
  or or_1 (or_1_out, and_17_out, and_16_out);
  or or_2 (or_2_out, aIns, destA);
  or or_3 (or_3_out, aluNg, aluZr);
  not not_2 (not_2_out, or_3_out);
  and and_18 (and_18_out, jmpGt, not_2_out);
  or or_4 (or_4_out, and_18_out, or_1_out);
  Register #(.Bits(16)) Dregister (.D(outM), .C(C), .en(destD), .Q(Dregister_q));
  Register #(.Bits(16)) ARegister (.D(multiplexer_1_out), .C(C), .en(or_2_out), .Q({Areg[15], addressM}));
  PC pc_1 (.inc(1'b1), .load(or_4_out), .reset(reset), .in({Areg[15], addressM}), .C(C), .out({pc_1_out[15], pc}));
  Multiplexer #(.Bits(16)) multiplexer_2 (.sel(srcM), .in_0({Areg[15], addressM}), .in_1(inM), .out(multiplexer_2_out));
  ALU alu_1 (
    .x(Dregister_q), .y(multiplexer_2_out), .zx(aluZx), .nx(aluNx), .f(aluF), .no(aluNo), .zy(aluZy),
    .ny(aluNy), .out(outM), .zr(aluZr), .ng(aluNg));

  // Other names for the same wires on the sheet: aluOut[15:0] = outM; Areg[14:0] = addressM; DataMemory[15:0] = inM;
  //   ins[15:0] = instruction; ins0 = instruction[0]; ins1 = instruction[1]; ins2 = instruction[2];
  //   ins3 = instruction[3]; ins4 = instruction[4]; ins5 = instruction[5]; ins6 = instruction[6];
  //   ins7 = instruction[7]; ins8 = instruction[8]; ins9 = instruction[9]; ins10 = instruction[10];
  //   ins11 = instruction[11]; ins12 = instruction[12]
endmodule
