// Digital circuit CPUplusMem.dig as structural Verilog
module CPUplusMem (
  input  reset,
  input  C,
  output [15:0] outM,
  output writeM,
  output [14:0] addressM,
  output [14:0] pc
);

  wire aIns, aluF, aluNg, aluNo, aluNx, aluNy, aluZr, aluZx, aluZy, and_1_out, and_16_out, and_17_out,
       and_18_out, cIns, destA, destD, jmpEq, jmpGt, jmpLt, not_2_out, or_1_out, or_2_out, or_3_out,
       or_4_out, srcM;
  wire [15:0] DataMemory, Dregister_q, ins, multiplexer_1_out, multiplexer_2_out;
  wire [15:15] Areg, pc_1_out;

  ROM #(.AddrBits(15), .isProgramMemory("true"), .Bits(16)) ProgramMemory (.A(pc), .sel(1'b1), .D(ins));
  and and_1 (and_1_out, ins[14], ins[15]);
  and and_2 (jmpGt, cIns, ins[0]);
  and and_3 (jmpEq, cIns, ins[1]);
  and and_4 (jmpLt, cIns, ins[2]);
  and and_5 (writeM, cIns, ins[3]);
  and and_6 (destD, cIns, ins[4]);
  and and_7 (destA, cIns, ins[5]);
  and and_8 (aluNo, cIns, ins[6]);
  and and_9 (aluF, cIns, ins[7]);
  and and_10 (aluNy, cIns, ins[8]);
  and and_11 (aluZy, cIns, ins[9]);
  and and_12 (aluNx, cIns, ins[10]);
  and and_13 (aluZx, cIns, ins[11]);
  and and_14 (srcM, ins[12], cIns);
  and and_15 (cIns, ins[13], and_1_out);
  not not_1 (aIns, ins[15]);
  and and_16 (and_16_out, jmpLt, aluNg);
  Multiplexer #(.Bits(16)) multiplexer_1 (.sel(aIns), .in_0(outM), .in_1(ins), .out(multiplexer_1_out));
  and and_17 (and_17_out, jmpEq, aluZr);
  or or_1 (or_1_out, and_17_out, and_16_out);
  or or_2 (or_2_out, aIns, destA);
  or or_3 (or_3_out, aluNg, aluZr);
  not not_2 (not_2_out, or_3_out);
  and and_18 (and_18_out, jmpGt, not_2_out);
  or or_4 (or_4_out, and_18_out, or_1_out);
  Register #(.Bits(16)) Dregister (.D(outM), .C(C), .en(destD), .Q(Dregister_q));
  Register #(.Bits(16)) ARegister (.D(multiplexer_1_out), .C(C), .en(or_2_out), .Q({Areg[15], addressM}));
  PC pc_1 (.inc(1'b1), .load(or_4_out), .reset(reset), .in({Areg[15], addressM}), .C(C), .out({pc_1_out[15], pc}));
  Multiplexer #(.Bits(16)) multiplexer_2 (
    .sel(srcM), .in_0({Areg[15], addressM}), .in_1(DataMemory), .out(multiplexer_2_out));
  ALU alu_1 (
    .x(Dregister_q), .y(multiplexer_2_out), .zx(aluZx), .nx(aluNx), .f(aluF), .no(aluNo), .zy(aluZy),
    .ny(aluNy), .out(outM), .zr(aluZr), .ng(aluNg));
  RAMDualPort #(.AddrBits(15), .Bits(16)) ramdualport_1 (
    .A(addressM), .Din(outM), .str(writeM), .C(C), .ld(1'b1), .D(DataMemory));

  // Other names for the same wires on the sheet: instructionAddress[14:0] = pc; aluOut[15:0] = outM;
  //   Areg[14:0] = addressM

  // Notes on the sheet:
  //   ProgramMemory loads p3.hex
endmodule
