// Digital circuit CPUplusMemDisplay.dig as structural Verilog
module CPUplusMemDisplay (
  input  reset,
  input  C,
  output [15:0] outM,
  output writeM,
  output [14:0] addressM,
  output [14:0] pc
);

  wire _1_out, aIns, aluF, aluNg, aluNo, aluNx, aluNy, aluZr, aluZx, aluZy, and_1_out, and_16_out,
       and_17_out, and_18_out, cIns, demultiplexer_1_out_0, demultiplexer_1_out_1, destA, destD, jmpEq,
       jmpGt, jmpLt, loadRAM, loadScreen, not_2_out, or_1_out, or_2_out, or_3_out, or_4_out, srcM;
  wire [15:0] DataMemory, Dregister_q, hackdisplay_1_p6, ins, mem_d, multiplexer_1_out, multiplexer_2_out,
       multiplexer_3_out;
  wire [15:15] Areg, pc_1_out;

  ROM #(.AddrBits(15), .Bits(16)) Program_Memory (.A(pc), .sel(1'b1), .D(ins));
  and and_1 (and_1_out, ins[14], ins[15]);
  and and_2 (jmpGt, cIns, ins[0]);
  and and_3 (jmpEq, cIns, ins[1]);
  and and_4 (jmpLt, cIns, ins[2]);
  and and_5 (writeM, cIns, ins[3]);
  and and_6 (destD, cIns, ins[4]);
  and and_7 (destA, cIns, ins[5]);
  and and_8 (aluNo, cIns, ins[6]);
  and and_9 (aluF, cIns, ins[7]);
  and and_10 (aluNy, cIns, ins[8]);
  and and_11 (aluZy, cIns, ins[9]);
  and and_12 (aluNx, cIns, ins[10]);
  and and_13 (aluZx, cIns, ins[11]);
  and and_14 (srcM, ins[12], cIns);
  and and_15 (cIns, ins[13], and_1_out);
  not not_1 (aIns, ins[15]);
  and and_16 (and_16_out, jmpLt, aluNg);
  Multiplexer #(.Bits(16)) multiplexer_1 (.sel(aIns), .in_0(outM), .in_1(ins), .out(multiplexer_1_out));
  and and_17 (and_17_out, jmpEq, aluZr);
  or or_1 (or_1_out, and_17_out, and_16_out);
  or or_2 (or_2_out, aIns, destA);
  or or_3 (or_3_out, aluNg, aluZr);
  not not_2 (not_2_out, or_3_out);
  and and_18 (and_18_out, jmpGt, not_2_out);
  or or_4 (or_4_out, and_18_out, or_1_out);
  Register #(.Bits(16)) Dregister (.D(outM), .C(C), .en(destD), .Q(Dregister_q));
  Register #(.Bits(16)) ARegister (.D(multiplexer_1_out), .C(C), .en(or_2_out), .Q({Areg[15], addressM}));
  PC pc_1 (.inc(1'b1), .load(or_4_out), .reset(reset), .in({Areg[15], addressM}), .C(C), .out({pc_1_out[15], pc}));
  Multiplexer #(.Bits(16)) multiplexer_2 (
    .sel(srcM), .in_0({Areg[15], addressM}), .in_1(DataMemory), .out(multiplexer_2_out));
  ALU alu_1 (
    .x(Dregister_q), .y(multiplexer_2_out), .zx(aluZx), .nx(aluNx), .f(aluF), .no(aluNo), .zy(aluZy),
    .ny(aluNy), .out(outM), .zr(aluZr), .ng(aluNg));
  Demultiplexer #(.Selector_Bits(2)) demultiplexer_1 (
    .sel(addressM[14:13]), .in(writeM), .out_0(demultiplexer_1_out_0), .out_1(demultiplexer_1_out_1),
    .out_2(loadScreen));  // open: out_3
  or or_5 (loadRAM, demultiplexer_1_out_0, demultiplexer_1_out_1);
  Button #(.activeLow("true")) _1 (.out(_1_out));
  RAMDualPort #(.AddrBits(15), .Bits(16)) mem (.A(addressM), .Din(outM), .str(loadRAM), .C(C), .ld(1'b1), .D(mem_d));
  // HackDisplay hackdisplay_1: pin names not known; wires that end beside it: addressM[12:0], outM, loadScreen, C, 1'b1, hackdisplay_1_p6
  // Probe on _1_out
  Multiplexer #(.Bits(16)) multiplexer_3 (.sel(_1_out), .in_0(16'h31), .in_1({16{1'b0}}), .out(multiplexer_3_out));
  Multiplexer #(.Selector_Bits(2), .Bits(16)) multiplexer_4 (
    .sel(addressM[14:13]), .in_0(mem_d), .in_1(mem_d), .in_2(hackdisplay_1_p6), .in_3(multiplexer_3_out),
    .out(DataMemory));

  // Other names for the same wires on the sheet: instructionAddress[14:0] = pc; Areg[14:0] = addressM;
  //   aluOut[15:0] = outM; outMemory[15:0] = outM

  // Notes on the sheet:
  //   C: Hz: 2147483647
  //   contents of Program_Memory (hex, n*v repeats v):
  //   3,4,5
endmodule

/* Test case test1:
C reset outM writeM addressM pc
memory mem(0)=50;
repeat(1000) C 0 X X X X
*/
