// Digital circuit Computer.dig as structural Verilog
module Computer (
  input  reset,
  input  C
);

  wire cpu_1_writem;
  wire [14:0] cpu_1_addressm, cpu_1_pc;
  wire [15:0] cpu_1_outm, ramdualport_1_d, rom_1_d;

  ROM #(.AddrBits(15), .Bits(16)) rom_1 (.A(cpu_1_pc), .sel(1'b1), .D(rom_1_d));
  CPU cpu_1 (
    .inM(ramdualport_1_d), .instruction(rom_1_d), .reset(reset), .outM(cpu_1_outm), .writeM(cpu_1_writem),
    .addressM(cpu_1_addressm), .pc(cpu_1_pc), .C(C));
  RAMDualPort #(.AddrBits(15), .Bits(16)) ramdualport_1 (
    .A(cpu_1_addressm), .Din(cpu_1_outm), .str(cpu_1_writem), .C(C), .ld(1'b1), .D(ramdualport_1_d));

  // Notes on the sheet:
  //   contents of rom_1 (hex, n*v repeats v):
  //   2,ec10,3,e090,0,e308
endmodule
