// Digital circuit PC.dig as structural Verilog
module PC (
  input  inc,
  input  load,
  input  reset,
  input  [15:0] in,
  input  C,
  output [15:0] out
);

  wire [15:0] incrementer_s, multiplexer_1_out, multiplexer_2_out, multiplexer_3_out;

  Add #(.Bits(16)) incrementer (.a(out), .b(16'h1), .c_i(1'b0), .s(incrementer_s));  // open: c_o
  Multiplexer #(.Bits(16)) multiplexer_1 (.sel(inc), .in_0(out), .in_1(incrementer_s), .out(multiplexer_1_out));
  Multiplexer #(.Bits(16)) multiplexer_2 (.sel(load), .in_0(multiplexer_1_out), .in_1(in), .out(multiplexer_2_out));
  Multiplexer #(.Bits(16)) multiplexer_3 (
    .sel(reset), .in_0(multiplexer_2_out), .in_1({16{1'b0}}), .out(multiplexer_3_out));
  Register #(.Bits(16)) register_1 (.D(multiplexer_3_out), .C(C), .en(1'b1), .Q(out));
endmodule
